// Logisim project aiAlu.circ as structural Verilog
module Half_Adder (
  input  a,
  input  b,
  output S,
  output C
);

  xor xor_1 (S, b, a);
  and and_1 (C, b, a);
endmodule

module Full_Adder (
  input  Cin,
  input  a,
  input  b,
  input  S,
  input  Cout
);

  wire and_1_out, and_2_out, and_3_out, xor_1_out;

  xor xor_1 (xor_1_out, a, b);
  and and_1 (and_1_out, Cin, a);
  and and_2 (and_2_out, a, b);
  and and_3 (and_3_out, Cin, b);
  xor xor_2 (S, xor_1_out, Cin);
  and and_4 (Cout, and_1_out, and_2_out, and_3_out);
endmodule

module Cpl_2 (
  input  [7:0] in_1,
  output C,
  output [7:0] out_3
);

  wire half_adder_1_c, half_adder_2_c, half_adder_3_c, half_adder_4_c, half_adder_5_c, half_adder_6_c,
       half_adder_8_c;
  wire [7:0] not_1_out;

  assign not_1_out = ~in_1;  // NOT_Gate not_1, 8 bits wide
  Half_Adder half_adder_1 (.S(out_3[0]), .C(half_adder_1_c), .a(1'b1), .b(not_1_out[0]));
  Half_Adder half_adder_2 (.S(out_3[2]), .C(half_adder_2_c), .a(not_1_out[2]), .b(half_adder_3_c));
  Half_Adder half_adder_3 (.S(out_3[1]), .C(half_adder_3_c), .a(not_1_out[1]), .b(half_adder_1_c));
  Half_Adder half_adder_4 (.S(out_3[4]), .C(half_adder_4_c), .a(not_1_out[4]), .b(half_adder_5_c));
  Half_Adder half_adder_5 (.S(out_3[3]), .C(half_adder_5_c), .a(not_1_out[3]), .b(half_adder_2_c));
  Half_Adder half_adder_6 (.S(out_3[5]), .C(half_adder_6_c), .a(not_1_out[5]), .b(half_adder_4_c));
  Half_Adder half_adder_7 (.S(out_3[7]), .C(C), .a(not_1_out[7]), .b(half_adder_8_c));
  Half_Adder half_adder_8 (.S(out_3[6]), .C(half_adder_8_c), .a(not_1_out[6]), .b(half_adder_6_c));
endmodule

module Adder_4_bits (
);

  Half_Adder half_adder_1 ();  // open: S, C, a, b
  Full_Adder full_adder_1 ();  // open: S, Cout, Cin, a, b
  Full_Adder full_adder_2 ();  // open: S, Cout, Cin, a, b
  Full_Adder full_adder_3 ();  // open: S, Cout, Cin, a, b
endmodule
